// Digital circuit example_circuit.dig as structural Verilog
module example_circuit (
  input  clk,
  input  input_1,
  input  input_0,
  input  reset,
  input  set,
  output output_1,
  output output_2,
  output output_3
);

  wire five__input__AND__gate__out, five__input__and__in1, five__input__and__in2, five__input__and__in3,
       five__input__and__in4, five__input__and__in5, five__input__OR__gate, five__input__or__in1,
       four__input__AND__gate__out, four__input__and__in1, four__input__and__in2, four__input__and__in3,
       four__input__and__in4, four__input__OR__gate, four__input__or__in1, nin_0, nin_1, nQ_0, nQ_1, nQ_2,
       Q_0, Q_0__plus, Q_1, Q_1__plus, Q_2, Q_2__plus, three__input__AND__gate__out, three__input__and__in1,
       three__input__and__in2, three__input__and__in3, three__input__OR__gate, three__input__or__in1,
       three__input__or__in2, three__input__or__in3, three__input__or__in4, three__input__or__in5,
       two__input__AND__gate__out, two__input__and__in1, two__input__and__in2, two__input__OR__gate,
       two__input__or__in1;

  not not_1 (nin_1, input_1);
  not not_2 (nin_0, input_0);
  and and_1 (two__input__AND__gate__out, two__input__and__in1, two__input__and__in2);
  and and_2 (three__input__AND__gate__out, three__input__and__in1, three__input__and__in2, three__input__and__in3);
  and and_3 (four__input__AND__gate__out, four__input__and__in1, four__input__and__in2, four__input__and__in3, four__input__and__in4);
  and and_4 (five__input__AND__gate__out, five__input__and__in1, five__input__and__in2, five__input__and__in3, five__input__and__in4, five__input__and__in5);
  and and_5 (two__input__AND__gate__out, two__input__and__in1, two__input__and__in2);
  and and_6 (three__input__AND__gate__out, three__input__and__in1, three__input__and__in2, three__input__and__in3);
  and and_7 (four__input__AND__gate__out, four__input__and__in1, four__input__and__in2, four__input__and__in3, four__input__and__in4);
  D_FF_AS u_Q_2 (.Set(set), .D(Q_2__plus), .C(clk), .Clr(reset), .Q(Q_2), .nQ(nQ_2));
  D_FF_AS u_Q_1 (.Set(set), .D(Q_1__plus), .C(clk), .Clr(reset), .Q(Q_1), .nQ(nQ_1));
  or or_1 (two__input__OR__gate, two__input__or__in1, two__input__or__in1);
  or or_2 (three__input__OR__gate, three__input__or__in1, three__input__or__in2, three__input__or__in3);
  or or_3 (four__input__OR__gate, four__input__or__in1, three__input__or__in2, three__input__or__in3, three__input__or__in4);
  or or_4 (five__input__OR__gate, five__input__or__in1, three__input__or__in2, three__input__or__in3, three__input__or__in4, three__input__or__in5);
  or or_5 (two__input__OR__gate, two__input__or__in1, two__input__or__in1);
  or or_6 (three__input__OR__gate, three__input__or__in1, three__input__or__in2, three__input__or__in3);
  D_FF_AS u_Q_0 (.Set(set), .D(Q_0__plus), .C(clk), .Clr(reset), .Q(Q_0), .nQ(nQ_0));
  Seven_Seg_Hex seven_seg_hex_1 (.d({1'b0, Q_2, Q_1, Q_0}), .dp(1'b0));

  // Other names for the same wires on the sheet: in_0 = input_0; in_1 = input_1; out_1 = output_1; out_2 = output_2;
  //   out_3 = output_3

  // Notes on the sheet:
  //   State Logic
  //   Output Logic
endmodule
